# Fritzing sketch petmoj-vanilla (saved by Fritzing 0.9.2b)
breadboards: 1

parts:
  U1 = attiny85 [package=dip]
  U2 = USB Connectors [package=usb-microb]

nets:
  N1: U1.Pin_4, U2.GND
  N2: U1.Pin_6, U2.D-
  N3: U1.Pin_7, U2.D+
  N4: U1.Pin_8, U2.VBUS
